// Logisim project finaltower.circ as structural Verilog: 14 circuits, main circuit Gray Code Counter 3 disk
module main (
);

  wire and_1_out, Clock_out, n2_disk_1_enable_next, n2_disk_1_enabler, n2_disk_1_out_5, n2_disk_1_out_6,
       n2_disk_1_out_7, n2_disk_1_out_8, n2_disk_1_out_9, n2_disk_1_out_10, n3_disk_1_enable_next,
       n3_disk_1_out_5, n3_disk_1_out_6, n3_disk_1_out_7, n3_disk_1_out_8, n3_disk_1_out_9, n3_disk_1_out_10,
       n3_disk_1_out_11, n3_disk_1_out_12, n3_disk_1_out_13, not_1_out, Reset_out;

  LED led_1 (.in(n3_disk_1_out_7));
  LED led_2 (.in(n3_disk_1_out_6));
  LED led_3 (.in(n3_disk_1_out_5));
  Button Clock (.out(Clock_out));
  Button Reset (.out(Reset_out));
  not not_1 (not_1_out, n3_disk_1_enable_next);
  LED led_4 (.in(n2_disk_1_out_5));
  LED led_5 (.in(n2_disk_1_out_6));
  and and_1 (and_1_out, Clock_out, not_1_out);
  LED led_6 (.in(n3_disk_1_out_8));
  LED led_7 (.in(n3_disk_1_out_9));
  LED led_8 (.in(n3_disk_1_out_10));
  LED led_9 (.in(n2_disk_1_out_7));
  LED led_10 (.in(n2_disk_1_out_8));
  _3_disk u_3_disk_1 (
    .Clock(and_1_out), .Enable(n2_disk_1_enable_next), .Reset(Reset_out), .out_5(n3_disk_1_out_5),
    .out_6(n3_disk_1_out_6), .out_7(n3_disk_1_out_7), .out_8(n3_disk_1_out_8), .out_9(n3_disk_1_out_9),
    .out_10(n3_disk_1_out_10), .out_11(n3_disk_1_out_11), .out_12(n3_disk_1_out_12),
    .out_13(n3_disk_1_out_13), .Enabler_prev(n2_disk_1_enabler), .Enable_next(n3_disk_1_enable_next));  // open: Enabler
  LED led_11 (.in(n3_disk_1_out_12));
  LED led_12 (.in(n3_disk_1_out_11));
  LED led_13 (.in(n2_disk_1_out_9));
  LED led_14 (.in(n3_disk_1_out_13));
  LED led_15 (.in(n2_disk_1_out_10));
  _2_disk u_2_disk_1 (
    .Clock(and_1_out), .Enable(1'b1), .Reset(Reset_out), .out_5(n2_disk_1_out_5), .out_6(n2_disk_1_out_6),
    .out_7(n2_disk_1_out_7), .out_8(n2_disk_1_out_8), .out_9(n2_disk_1_out_9), .out_10(n2_disk_1_out_10),
    .Enabler_prev(1'b1), .Enabler(n2_disk_1_enabler), .Enable_next(n2_disk_1_enable_next));
endmodule

module another_main (
);

  wire and_1_out, Clock_out, n2_disk_1_enable_next, n2_disk_1_out_5, n2_disk_1_out_6, n2_disk_1_out_7,
       n2_disk_1_out_8, n2_disk_1_out_9, n2_disk_1_out_10, n2_disk_2_enable_next, n2_disk_2_enabler,
       n2_disk_2_out_5, n2_disk_2_out_6, n2_disk_2_out_7, n2_disk_2_out_8, n2_disk_2_out_9, n2_disk_2_out_10,
       n2_disk_3_enable_next, n2_disk_3_enabler, n2_disk_3_out_5, n2_disk_3_out_6, n2_disk_3_out_7,
       n2_disk_3_out_8, n2_disk_3_out_9, n2_disk_3_out_10, not_1_out, Reset_out;

  LED led_1 (.in(n2_disk_1_out_5));
  LED led_2 (.in(n2_disk_1_out_6));
  LED led_3 (.in(n2_disk_2_out_5));
  Button Clock (.out(Clock_out));
  Button Reset (.out(Reset_out));
  LED led_4 (.in(n2_disk_3_out_6));
  LED led_5 (.in(n2_disk_2_out_6));
  LED led_6 (.in(n2_disk_3_out_5));
  and and_1 (and_1_out, Clock_out, not_1_out);
  not not_1 (not_1_out, n2_disk_1_enable_next);
  LED led_7 (.in(n2_disk_2_out_7));
  LED led_8 (.in(n2_disk_1_out_7));
  LED led_9 (.in(n2_disk_1_out_8));
  _2_disk u_2_disk_1 (
    .Clock(and_1_out), .Enable(n2_disk_2_enable_next), .Reset(Reset_out), .out_5(n2_disk_1_out_5),
    .out_6(n2_disk_1_out_6), .out_7(n2_disk_1_out_7), .out_8(n2_disk_1_out_8), .out_9(n2_disk_1_out_9),
    .out_10(n2_disk_1_out_10), .Enabler_prev(n2_disk_2_enabler), .Enable_next(n2_disk_1_enable_next));  // open: Enabler
  LED led_10 (.in(n2_disk_3_out_8));
  LED led_11 (.in(n2_disk_2_out_8));
  LED led_12 (.in(n2_disk_3_out_7));
  LED led_13 (.in(n2_disk_1_out_9));
  _2_disk u_2_disk_2 (
    .Clock(and_1_out), .Enable(n2_disk_3_enable_next), .Reset(Reset_out), .out_5(n2_disk_2_out_5),
    .out_6(n2_disk_2_out_6), .out_7(n2_disk_2_out_7), .out_8(n2_disk_2_out_8), .out_9(n2_disk_2_out_9),
    .out_10(n2_disk_2_out_10), .Enabler_prev(n2_disk_3_enabler), .Enabler(n2_disk_2_enabler),
    .Enable_next(n2_disk_2_enable_next));
  LED led_14 (.in(n2_disk_1_out_10));
  LED led_15 (.in(n2_disk_2_out_10));
  LED led_16 (.in(n2_disk_3_out_9));
  LED led_17 (.in(n2_disk_2_out_9));
  LED led_18 (.in(n2_disk_3_out_10));
  _2_disk u_2_disk_3 (
    .Clock(and_1_out), .Enable(1'b1), .Reset(Reset_out), .out_5(n2_disk_3_out_5), .out_6(n2_disk_3_out_6),
    .out_7(n2_disk_3_out_7), .out_8(n2_disk_3_out_8), .out_9(n2_disk_3_out_9), .out_10(n2_disk_3_out_10),
    .Enabler_prev(1'b1), .Enabler(n2_disk_3_enabler), .Enable_next(n2_disk_3_enable_next));
endmodule

module Peg (
  input  Clock,
  input  Clear,
  output Peg_1,
  output Peg_2,
  output Peg_3
);

  D_Flip_Flop d_ff_1 (.clk(Clock), .D(Peg_3), .Q(Peg_1), .reset(Clear));  // open: Qn, preset, en
  D_Flip_Flop d_ff_2 (.clk(Clock), .D(Peg_1), .Q(Peg_2), .preset(Clear));  // open: Qn, en, reset
  D_Flip_Flop d_ff_3 (.clk(Clock), .D(Peg_2), .Q(Peg_3), .preset(Clear));  // open: Qn, en, reset
endmodule

module Gray_Code_Counter_3_disk (
  input  Clock,
  input  Reset,
  input  Enable,
  output Q2,
  output Q1,
  output Q0
);

  wire d_ff_1_q, d_ff_1_qn, d_ff_2_q, d_ff_2_qn, d_ff_3_qn;

  D_Flip_Flop d_ff_1 (
    .clk(Clock), .D(d_ff_1_qn), .Q(d_ff_1_q), .Qn(d_ff_1_qn), .en(Enable), .reset(Reset));  // open: preset
  D_Flip_Flop d_ff_2 (
    .clk(d_ff_1_qn), .D(d_ff_2_qn), .Q(d_ff_2_q), .Qn(d_ff_2_qn), .en(Enable), .reset(Reset));  // open: preset
  D_Flip_Flop d_ff_3 (
    .clk(d_ff_2_qn), .D(d_ff_3_qn), .Q(Q2), .Qn(d_ff_3_qn), .en(Enable), .reset(Reset));  // open: preset
  xor xor_1 (Q1, d_ff_2_q, Q2);
  xor xor_2 (Q0, d_ff_2_q, d_ff_1_q);
endmodule

module PIPO_Shift_Register_3_disk (
  input  Clock,
  input  I2,
  input  I1,
  input  I0,
  input  Clear,
  input  Enable,
  output Q2,
  output Q1,
  output Q0
);

  D_Flip_Flop d_ff_1 (.clk(Clock), .D(I2), .Q(Q2), .en(Enable), .reset(Clear));  // open: Qn, preset
  D_Flip_Flop d_ff_2 (.clk(Clock), .D(I1), .Q(Q1), .en(Enable), .reset(Clear));  // open: Qn, preset
  D_Flip_Flop d_ff_3 (.clk(Clock), .D(I0), .Q(Q0), .en(Enable), .reset(Clear));  // open: Qn, preset
endmodule

module Disk_Size_3_disk (
  input  Clock,
  input  Clear,
  input  Enable,
  output Disk_Large,
  output Disk_Medium,
  output Disk_Small
);

  wire Gray_Code_Counter_q0, Gray_Code_Counter_q1, Gray_Code_Counter_q2, PIPO_Shift_Register_q0,
       PIPO_Shift_Register_q1, PIPO_Shift_Register_q2;

  Gray_Code_Counter_3_disk Gray_Code_Counter (
    .Clock(Clock), .Reset(Clear), .Enable(Enable), .Q2(Gray_Code_Counter_q2), .Q1(Gray_Code_Counter_q1),
    .Q0(Gray_Code_Counter_q0));
  xor xor_1 (Disk_Large, Gray_Code_Counter_q2, PIPO_Shift_Register_q2);
  xor xor_2 (Disk_Medium, Gray_Code_Counter_q1, PIPO_Shift_Register_q1);
  PIPO_Shift_Register_3_disk PIPO_Shift_Register (
    .Clock(Clock), .I2(Gray_Code_Counter_q2), .I1(Gray_Code_Counter_q1), .I0(Gray_Code_Counter_q0),
    .Clear(Clear), .Enable(Enable), .Q2(PIPO_Shift_Register_q2), .Q1(PIPO_Shift_Register_q1),
    .Q0(PIPO_Shift_Register_q0));
  xor xor_3 (Disk_Small, Gray_Code_Counter_q0, PIPO_Shift_Register_q0);
endmodule

module Move_counter_3_disk (
  input  Clock,
  input  Reset,
  input  Enable,
  output Q0,
  output Q1,
  output Q2
);

  wire and_1_out;

  T_Flip_Flop t_ff_1 (.clk(Clock), .T(1'b1), .Q(Q0), .reset(Reset), .en(Enable));  // open: Qn, preset
  T_Flip_Flop t_ff_2 (.clk(Clock), .T(Q0), .Q(Q1), .reset(Reset), .en(Enable));  // open: Qn, preset
  and and_1 (and_1_out, Q1, Q0);
  T_Flip_Flop t_ff_3 (.clk(Clock), .T(and_1_out), .Q(Q2), .reset(Reset), .en(Enable));  // open: Qn, preset
endmodule

module _3_disk (
  input  Enabler_prev,
  input  Clock,
  input  Enable,
  input  Reset,
  output out_5,
  output out_6,
  output out_7,
  output out_8,
  output out_9,
  output out_10,
  output out_11,
  output out_12,
  output out_13,
  output Enabler,
  output Enable_next
);

  wire and_1_out, and_2_out, and_3_out, and_4_out, and_5_out, and_6_out, and_7_out, and_8_out, and_9_out,
       and_10_out, and_11_out, and_12_out, and_13_out, and_15_out, Disk_finder_disk_large,
       Disk_finder_disk_medium, Disk_finder_disk_small, Extender_enable_prev, Move_counter_q0,
       Move_counter_q1, Move_counter_q2, not_1_out, not_2_out, or_1_out, or_2_out, Peg_finder_peg_1,
       Peg_finder_peg_2, Peg_finder_peg_3;

  not not_1 (not_1_out, Clock);
  and and_1 (and_1_out, Enable, Extender_enable_prev);
  T_Flip_Flop t_ff_1 (.clk(not_1_out), .T(and_3_out), .Q(out_6), .preset(Reset));  // open: Qn, reset, en
  T_Flip_Flop t_ff_2 (.clk(not_1_out), .T(and_2_out), .Q(out_5), .preset(Reset));  // open: Qn, reset, en
  and and_2 (and_2_out, Disk_finder_disk_large, and_8_out);
  and and_3 (and_3_out, Disk_finder_disk_medium, and_8_out);
  Peg Peg_finder (
    .Clock(Clock), .Clear(Reset), .Peg_1(Peg_finder_peg_1), .Peg_2(Peg_finder_peg_2), .Peg_3(Peg_finder_peg_3));
  T_Flip_Flop t_ff_3 (.clk(not_1_out), .T(and_4_out), .Q(out_7), .preset(Reset));  // open: Qn, reset, en
  and and_4 (and_4_out, Disk_finder_disk_small, and_8_out);
  Disk_Size_3_disk Disk_finder (
    .Clock(Clock), .Clear(or_1_out), .Enable(and_1_out), .Disk_Large(Disk_finder_disk_large),
    .Disk_Medium(Disk_finder_disk_medium), .Disk_Small(Disk_finder_disk_small));
  or or_1 (or_1_out, Reset, and_15_out);
  T_Flip_Flop t_ff_4 (.clk(not_1_out), .T(and_5_out), .Q(out_8), .reset(Reset));  // open: Qn, preset, en
  and and_5 (and_5_out, Disk_finder_disk_large, and_9_out);
  T_Flip_Flop t_ff_5 (.clk(not_1_out), .T(and_6_out), .Q(out_9), .reset(Reset));  // open: Qn, preset, en
  and and_6 (and_6_out, Disk_finder_disk_medium, and_9_out);
  and and_7 (and_7_out, Disk_finder_disk_small, and_9_out);
  and and_8 (and_8_out, and_1_out, Peg_finder_peg_1);
  T_Flip_Flop t_ff_6 (.clk(not_1_out), .T(and_7_out), .Q(out_10), .reset(Reset));  // open: Qn, preset, en
  and and_9 (and_9_out, and_1_out, Peg_finder_peg_2);
  T_Flip_Flop t_ff_7 (.clk(not_1_out), .T(and_10_out), .Q(out_11), .reset(Reset));  // open: Qn, preset, en
  and and_10 (and_10_out, Disk_finder_disk_large, and_12_out);
  and and_11 (and_11_out, Disk_finder_disk_medium, and_12_out);
  and and_12 (and_12_out, and_1_out, Peg_finder_peg_3);
  T_Flip_Flop t_ff_8 (.clk(not_1_out), .T(and_11_out), .Q(out_12), .reset(Reset));  // open: Qn, preset, en
  and and_13 (and_13_out, Disk_finder_disk_small, and_12_out);
  T_Flip_Flop t_ff_9 (.clk(not_1_out), .T(and_13_out), .Q(out_13), .reset(Reset));  // open: Qn, preset, en
  not not_2 (not_2_out, not_1_out);
  and and_14 (Enabler, and_15_out, Enabler_prev);
  and and_15 (and_15_out, Move_counter_q0, Move_counter_q1, Move_counter_q2);
  Move_counter_3_disk Move_counter (
    .Clock(not_1_out), .Reset(or_2_out), .Enable(and_1_out), .Q0(Move_counter_q0), .Q1(Move_counter_q1),
    .Q2(Move_counter_q2));
  Extender Extender (
    .Clock(not_2_out), .Reset(Reset), .Enabler(Enabler), .Enable_next(Enable_next),
    .Enable_prev(Extender_enable_prev));
  or or_2 (or_2_out, Reset, Enable_next);
endmodule

module Gray_Code_Counter_2_disk (
  input  Clock,
  input  Reset,
  input  Enable,
  output Q2,
  output Q1
);

  wire d_ff_1_q, d_ff_1_qn, d_ff_2_qn;

  D_Flip_Flop d_ff_1 (
    .clk(Clock), .D(d_ff_1_qn), .Q(d_ff_1_q), .Qn(d_ff_1_qn), .en(Enable), .reset(Reset));  // open: preset
  D_Flip_Flop d_ff_2 (
    .clk(d_ff_1_qn), .D(d_ff_2_qn), .Q(Q2), .Qn(d_ff_2_qn), .en(Enable), .reset(Reset));  // open: preset
  xor xor_1 (Q1, d_ff_1_q, Q2);
endmodule

module PIPO_Shift_Register_2_disk (
  input  Clock,
  input  I1,
  input  I0,
  input  Clear,
  input  Enable,
  output Q1,
  output Q0
);

  D_Flip_Flop d_ff_1 (.clk(Clock), .D(I1), .Q(Q1), .en(Enable), .reset(Clear));  // open: Qn, preset
  D_Flip_Flop d_ff_2 (.clk(Clock), .D(I0), .Q(Q0), .en(Enable), .reset(Clear));  // open: Qn, preset
endmodule

module Disk_Size_2_disk (
  input  Clock,
  input  Clear,
  input  Enable,
  output Disk_Medium,
  output Disk_Small
);

  wire Gray_Code_Counter_q1, Gray_Code_Counter_q2, PIPO_Shift_Register_q0, PIPO_Shift_Register_q1;

  Gray_Code_Counter_2_disk Gray_Code_Counter (
    .Clock(Clock), .Reset(Clear), .Enable(Enable), .Q2(Gray_Code_Counter_q2), .Q1(Gray_Code_Counter_q1));
  xor xor_1 (Disk_Medium, Gray_Code_Counter_q2, PIPO_Shift_Register_q1);
  PIPO_Shift_Register_2_disk PIPO_Shift_Register (
    .Clock(Clock), .I1(Gray_Code_Counter_q2), .I0(Gray_Code_Counter_q1), .Clear(Clear), .Enable(Enable),
    .Q1(PIPO_Shift_Register_q1), .Q0(PIPO_Shift_Register_q0));
  xor xor_2 (Disk_Small, Gray_Code_Counter_q1, PIPO_Shift_Register_q0);
endmodule

module Move_counter_2_disk (
  input  Clock,
  input  Reset,
  input  Enable,
  output Q0,
  output Q1
);

  T_Flip_Flop t_ff_1 (.clk(Clock), .T(1'b1), .Q(Q0), .reset(Reset), .en(Enable));  // open: Qn, preset
  T_Flip_Flop t_ff_2 (.clk(Clock), .T(Q0), .Q(Q1), .reset(Reset), .en(Enable));  // open: Qn, preset
endmodule

module _2_disk (
  input  Enabler_prev,
  input  Clock,
  input  Enable,
  input  Reset,
  output out_5,
  output out_6,
  output out_7,
  output out_8,
  output out_9,
  output out_10,
  output Enabler,
  output Enable_next
);

  wire and_1_out, and_2_out, and_3_out, and_4_out, and_5_out, and_6_out, and_7_out, and_8_out, and_9_out,
       and_10_out, and_12_out, Disk_finder_disk_medium, Disk_finder_disk_small, Extender_enable_prev,
       Move_Counter_q0, Move_Counter_q1, not_1_out, not_2_out, or_1_out, or_2_out, Peg_finder_peg_1,
       Peg_finder_peg_2, Peg_finder_peg_3;

  and and_1 (and_1_out, Enable, Extender_enable_prev);
  not not_1 (not_1_out, Clock);
  Peg Peg_finder (
    .Clock(Clock), .Clear(Reset), .Peg_1(Peg_finder_peg_1), .Peg_2(Peg_finder_peg_2), .Peg_3(Peg_finder_peg_3));
  T_Flip_Flop t_ff_1 (.clk(not_1_out), .T(and_2_out), .Q(out_5), .preset(Reset));  // open: Qn, reset, en
  and and_2 (and_2_out, Disk_finder_disk_medium, and_7_out);
  T_Flip_Flop t_ff_2 (.clk(not_1_out), .T(and_3_out), .Q(out_6), .preset(Reset));  // open: Qn, reset, en
  and and_3 (and_3_out, Disk_finder_disk_small, and_7_out);
  or or_1 (or_1_out, and_12_out, Reset);
  T_Flip_Flop t_ff_3 (.clk(not_1_out), .T(and_4_out), .Q(out_7), .reset(Reset));  // open: Qn, preset, en
  and and_4 (and_4_out, Disk_finder_disk_medium, and_9_out);
  Disk_Size_2_disk Disk_finder (
    .Clock(Clock), .Clear(or_1_out), .Enable(and_1_out), .Disk_Medium(Disk_finder_disk_medium),
    .Disk_Small(Disk_finder_disk_small));
  T_Flip_Flop t_ff_4 (.clk(not_1_out), .T(and_5_out), .Q(out_8), .reset(Reset));  // open: Qn, preset, en
  and and_5 (and_5_out, Disk_finder_disk_small, and_9_out);
  and and_6 (and_6_out, Disk_finder_disk_medium, and_10_out);
  and and_7 (and_7_out, and_1_out, Peg_finder_peg_1);
  T_Flip_Flop t_ff_5 (.clk(not_1_out), .T(and_6_out), .Q(out_9), .reset(Reset));  // open: Qn, preset, en
  and and_8 (and_8_out, Disk_finder_disk_small, and_10_out);
  and and_9 (and_9_out, and_1_out, Peg_finder_peg_2);
  T_Flip_Flop t_ff_6 (.clk(not_1_out), .T(and_8_out), .Q(out_10), .reset(Reset));  // open: Qn, preset, en
  and and_10 (and_10_out, and_1_out, Peg_finder_peg_3);
  not not_2 (not_2_out, not_1_out);
  and and_11 (Enabler, and_12_out, Enabler_prev);
  and and_12 (and_12_out, Move_Counter_q0, Move_Counter_q1);
  Move_counter_2_disk Move_Counter (
    .Clock(not_1_out), .Reset(or_2_out), .Enable(and_1_out), .Q0(Move_Counter_q0), .Q1(Move_Counter_q1));
  Extender Extender (
    .Clock(not_2_out), .Reset(Reset), .Enabler(Enabler), .Enable_next(Enable_next),
    .Enable_prev(Extender_enable_prev));
  or or_2 (or_2_out, Reset, Enable_next);
endmodule

module Extender (
  input  Clock,
  input  Reset,
  input  Enabler,
  output Enable_next,
  output Enable_prev
);

  wire and_1_out, not_1_out, or_1_out;

  not not_1 (not_1_out, Clock);
  and and_1 (and_1_out, Enable_next, not_1_out);
  or or_1 (or_1_out, and_1_out, Enabler);
  T_Flip_Flop t_ff_1 (.clk(or_1_out), .T(1'b1), .Q(Enable_next), .Qn(Enable_prev), .reset(Reset));  // open: preset, en
endmodule
