// Logisim project towerofhanoi.circ as structural Verilog: 14 circuits, main circuit Gray Code Counter 3 disk
module main (
);

  wire and_1_out, Clock_out, n2_disk_1_out_7, n2_disk_1_out_8, n2_disk_1_out_9, n2_disk_1_out_10,
       n2_disk_1_out_11, n2_disk_1_out_12, n2_disk_2_out_7, n2_disk_2_out_8, n2_disk_2_out_9,
       n2_disk_2_out_10, n2_disk_2_out_11, n2_disk_2_out_12, n2_disk_2_out_13, not_1_out, not_2_out,
       or_1_out, peg_1_peg_1, peg_1_peg_2, peg_1_peg_3, Reset_out, t_ff_1_q, t_ff_1_qn;

  LED led_1 (.in(n2_disk_1_out_7));
  LED led_2 (.in(n2_disk_1_out_8));
  LED led_3 (.in(n2_disk_2_out_8));
  LED led_4 (.in(n2_disk_2_out_7));
  Clock Clock (.out(Clock_out));
  Button Reset (.out(Reset_out));
  Peg peg_1 (
    .Clock(Clock_out), .Clear(Reset_out), .Peg_1(peg_1_peg_1), .Peg_2(peg_1_peg_2), .Peg_3(peg_1_peg_3),
    .Preset_1(not_2_out), .Preset_0(not_2_out));  // open: Enable, Preset_2
  not not_1 (not_1_out, Reset_out);
  and and_1 (and_1_out, t_ff_1_q, Clock_out);
  not not_2 (not_2_out, not_1_out);
  LED led_5 (.in(n2_disk_1_out_10));
  LED led_6 (.in(n2_disk_1_out_9));
  LED led_7 (.in(n2_disk_2_out_9));
  _2_disk u_2_disk_1 (
    .Clock(Clock_out), .Enable(t_ff_1_q), .Reset(Reset_out), .out_7(n2_disk_1_out_7),
    .out_8(n2_disk_1_out_8), .out_9(n2_disk_1_out_9), .out_10(n2_disk_1_out_10), .out_11(n2_disk_1_out_11),
    .out_12(n2_disk_1_out_12), .in_4(peg_1_peg_1), .in_3(peg_1_peg_2), .in_5(peg_1_peg_3));  // open: out_13
  LED led_8 (.in(n2_disk_2_out_10));
  or or_1 (or_1_out, and_1_out, n2_disk_2_out_13);
  T_Flip_Flop t_ff_1 (.clk(or_1_out), .T(1'b1), .Q(t_ff_1_q), .Qn(t_ff_1_qn), .reset(Reset_out));  // open: preset, en
  LED led_9 (.in(n2_disk_1_out_11));
  LED led_10 (.in(n2_disk_1_out_12));
  LED led_11 (.in(n2_disk_2_out_12));
  LED led_12 (.in(n2_disk_2_out_11));
  _2_disk u_2_disk_2 (
    .Clock(Clock_out), .Enable(t_ff_1_qn), .Reset(Reset_out), .out_7(n2_disk_2_out_7),
    .out_8(n2_disk_2_out_8), .out_9(n2_disk_2_out_9), .out_10(n2_disk_2_out_10), .out_11(n2_disk_2_out_11),
    .out_12(n2_disk_2_out_12), .in_4(peg_1_peg_1), .in_3(peg_1_peg_2), .in_5(peg_1_peg_3),
    .out_13(n2_disk_2_out_13));
endmodule

module Gray_Code_Counter_3_disk (
  input  Clock,
  input  Reset,
  output Q2,
  output Q1,
  output Q0
);

  wire d_ff_1_q, d_ff_1_qn, d_ff_2_q, d_ff_2_qn, d_ff_3_qn;

  D_Flip_Flop d_ff_1 (.clk(Clock), .D(d_ff_1_qn), .Q(d_ff_1_q), .Qn(d_ff_1_qn), .reset(Reset));  // open: preset, en
  D_Flip_Flop d_ff_2 (.clk(d_ff_1_qn), .D(d_ff_2_qn), .Q(d_ff_2_q), .Qn(d_ff_2_qn), .reset(Reset));  // open: preset, en
  D_Flip_Flop d_ff_3 (.clk(d_ff_2_qn), .D(d_ff_3_qn), .Q(Q2), .Qn(d_ff_3_qn), .reset(Reset));  // open: preset, en
  xor xor_1 (Q1, d_ff_2_q, Q2);
  xor xor_2 (Q0, d_ff_2_q, d_ff_1_q);
endmodule

module PIPO_Shift_Register_3_disk (
  input  Clock,
  input  I2,
  input  I1,
  input  I0,
  input  Clear,
  output Q2,
  output Q1,
  output Q0
);

  D_Flip_Flop d_ff_1 (.clk(Clock), .D(I2), .Q(Q2), .reset(Clear));  // open: Qn, preset, en
  D_Flip_Flop d_ff_2 (.clk(Clock), .D(I1), .Q(Q1), .reset(Clear));  // open: Qn, preset, en
  D_Flip_Flop d_ff_3 (.clk(Clock), .D(I0), .Q(Q0), .reset(Clear));  // open: Qn, preset, en
endmodule

module Disk_Size_3_disk (
  input  Clock,
  input  Clear,
  output Disk_Large,
  output Disk_Medium,
  output Disk_Small
);

  wire Gray_Code_Counter_q0, Gray_Code_Counter_q1, Gray_Code_Counter_q2, PIPO_Shift_Register_q0,
       PIPO_Shift_Register_q1, PIPO_Shift_Register_q2;

  Gray_Code_Counter_3_disk Gray_Code_Counter (
    .Clock(Clock), .Reset(Clear), .Q2(Gray_Code_Counter_q2), .Q1(Gray_Code_Counter_q1),
    .Q0(Gray_Code_Counter_q0));
  xor xor_1 (Disk_Large, Gray_Code_Counter_q2, PIPO_Shift_Register_q2);
  xor xor_2 (Disk_Medium, Gray_Code_Counter_q1, PIPO_Shift_Register_q1);
  PIPO_Shift_Register_3_disk PIPO_Shift_Register (
    .Clock(Clock), .I2(Gray_Code_Counter_q2), .I1(Gray_Code_Counter_q1), .I0(Gray_Code_Counter_q0),
    .Clear(Clear), .Q2(PIPO_Shift_Register_q2), .Q1(PIPO_Shift_Register_q1), .Q0(PIPO_Shift_Register_q0));
  xor xor_3 (Disk_Small, Gray_Code_Counter_q0, PIPO_Shift_Register_q0);
endmodule

module Peg (
  input  Clock,
  input  Clear,
  input  Enable,
  input  Preset_2,
  input  Preset_1,
  input  Preset_0,
  output Peg_1,
  output Peg_2,
  output Peg_3
);

  D_Flip_Flop d_ff_1 (.clk(Clock), .D(Peg_3), .Q(Peg_1), .preset(Preset_2), .en(Enable), .reset(Clear));  // open: Qn
  D_Flip_Flop d_ff_2 (.clk(Clock), .D(Peg_1), .Q(Peg_2), .preset(Preset_1), .en(Enable), .reset(Clear));  // open: Qn
  D_Flip_Flop d_ff_3 (.clk(Clock), .D(Peg_2), .Q(Peg_3), .preset(Preset_0), .en(Enable), .reset(Clear));  // open: Qn
endmodule

module _3_disk (
  input  Clock,
  input  Enable,
  input  Reset,
  input  in_4,
  input  in_5,
  input  in_6,
  output out_7,
  output out_8,
  output out_9,
  output out_10,
  output out_11,
  output out_12,
  output out_13,
  output out_14,
  output out_15
);

  wire and_1_out, and_2_out, and_3_out, and_4_out, and_5_out, and_6_out, and_7_out, and_8_out, and_9_out,
       and_10_out, disk_size_3_disk_1_disk_large, disk_size_3_disk_1_disk_medium,
       disk_size_3_disk_1_disk_small, not_1_out, not_2_out, peg_1_peg_1, peg_1_peg_2, peg_1_peg_3;

  and and_1 (and_1_out, Clock, Enable);
  T_Flip_Flop t_ff_1 (.clk(and_1_out), .T(and_2_out), .Q(out_8), .preset(Reset));  // open: Qn, reset, en
  T_Flip_Flop t_ff_2 (.clk(and_1_out), .T(and_3_out), .Q(out_7), .preset(Reset));  // open: Qn, reset, en
  and and_2 (and_2_out, disk_size_3_disk_1_disk_medium, peg_1_peg_1);
  and and_3 (and_3_out, disk_size_3_disk_1_disk_large, peg_1_peg_1);
  T_Flip_Flop t_ff_3 (.clk(and_1_out), .T(and_4_out), .Q(out_9), .preset(Reset));  // open: Qn, reset, en
  and and_4 (and_4_out, disk_size_3_disk_1_disk_small, peg_1_peg_1);
  Disk_Size_3_disk disk_size_3_disk_1 (
    .Clock(and_1_out), .Clear(Reset), .Disk_Large(disk_size_3_disk_1_disk_large),
    .Disk_Medium(disk_size_3_disk_1_disk_medium), .Disk_Small(disk_size_3_disk_1_disk_small));
  T_Flip_Flop t_ff_4 (.clk(and_1_out), .T(and_5_out), .Q(out_10), .reset(Reset));  // open: Qn, preset, en
  and and_5 (and_5_out, disk_size_3_disk_1_disk_large, peg_1_peg_2);
  T_Flip_Flop t_ff_5 (.clk(and_1_out), .T(and_6_out), .Q(out_11), .reset(Reset));  // open: Qn, preset, en
  and and_6 (and_6_out, disk_size_3_disk_1_disk_medium, peg_1_peg_2);
  and and_7 (and_7_out, disk_size_3_disk_1_disk_small, peg_1_peg_2);
  T_Flip_Flop t_ff_6 (.clk(and_1_out), .T(and_7_out), .Q(out_12), .reset(Reset));  // open: Qn, preset, en
  not not_1 (not_1_out, Reset);
  not not_2 (not_2_out, not_1_out);
  T_Flip_Flop t_ff_7 (.clk(and_1_out), .T(and_8_out), .Q(out_13), .reset(Reset));  // open: Qn, preset, en
  and and_8 (and_8_out, disk_size_3_disk_1_disk_large, peg_1_peg_3);
  and and_9 (and_9_out, disk_size_3_disk_1_disk_medium, peg_1_peg_3);
  Peg peg_1 (
    .Clock(and_1_out), .Clear(Reset), .Peg_1(peg_1_peg_1), .Peg_2(peg_1_peg_2), .Peg_3(peg_1_peg_3),
    .Preset_2(in_4), .Preset_1(in_5), .Preset_0(in_6));  // open: Enable
  T_Flip_Flop t_ff_8 (.clk(and_1_out), .T(and_9_out), .Q(out_14), .reset(Reset));  // open: Qn, preset, en
  and and_10 (and_10_out, disk_size_3_disk_1_disk_small, peg_1_peg_3);
  T_Flip_Flop t_ff_9 (.clk(and_1_out), .T(and_10_out), .Q(out_15), .reset(Reset));  // open: Qn, preset, en
endmodule

module _2_disk (
  input  Clock,
  input  Enable,
  input  in_3,
  input  in_4,
  input  in_5,
  input  Reset,
  output out_7,
  output out_8,
  output out_9,
  output out_10,
  output out_11,
  output out_12,
  output out_13
);

  wire and_1_out, and_2_out, and_3_out, and_4_out, and_5_out, and_6_out, and_7_out, and_8_out, and_9_out,
       and_11_out, and_12_out, delay_1_delayed_clock, disk_size_2_disk_1_disk_medium,
       disk_size_2_disk_1_disk_small, move_counter_2_disk_1_q0, move_counter_2_disk_1_q1, not_1_out, or_1_out;

  Delay delay_1 (.Clock(Clock), .Delayed_Clock(delay_1_delayed_clock));
  T_Flip_Flop t_ff_1 (.clk(delay_1_delayed_clock), .T(and_1_out), .Q(out_7), .preset(Reset));  // open: Qn, reset, en
  and and_1 (and_1_out, disk_size_2_disk_1_disk_medium, and_6_out);
  T_Flip_Flop t_ff_2 (.clk(delay_1_delayed_clock), .T(and_2_out), .Q(out_8), .preset(Reset));  // open: Qn, reset, en
  and and_2 (and_2_out, disk_size_2_disk_1_disk_small, and_6_out);
  T_Flip_Flop t_ff_3 (.clk(delay_1_delayed_clock), .T(and_3_out), .Q(out_9), .reset(Reset));  // open: Qn, preset, en
  and and_3 (and_3_out, disk_size_2_disk_1_disk_medium, and_8_out);
  Disk_Size_2_disk disk_size_2_disk_1 (
    .Clock(Clock), .Clear(Reset), .Enable(Enable), .Disk_Medium(disk_size_2_disk_1_disk_medium),
    .Disk_Small(disk_size_2_disk_1_disk_small));
  T_Flip_Flop t_ff_4 (.clk(delay_1_delayed_clock), .T(and_4_out), .Q(out_10), .reset(Reset));  // open: Qn, preset, en
  and and_4 (and_4_out, disk_size_2_disk_1_disk_small, and_8_out);
  and and_5 (and_5_out, disk_size_2_disk_1_disk_medium, and_9_out);
  and and_6 (and_6_out, Enable, in_4);
  T_Flip_Flop t_ff_5 (.clk(delay_1_delayed_clock), .T(and_5_out), .Q(out_11), .reset(Reset));  // open: Qn, preset, en
  and and_7 (and_7_out, disk_size_2_disk_1_disk_small, and_9_out);
  and and_8 (and_8_out, Enable, in_3);
  T_Flip_Flop t_ff_6 (.clk(delay_1_delayed_clock), .T(and_7_out), .Q(out_12), .reset(Reset));  // open: Qn, preset, en
  and and_9 (and_9_out, Enable, in_5);
  // AND_Gate and_10 has open pins: in0=out_9, in1=out_10, out=open
  not not_1 (not_1_out, delay_1_delayed_clock);
  and and_11 (and_11_out, move_counter_2_disk_1_q0, move_counter_2_disk_1_q1);
  Move_counter_2_disk move_counter_2_disk_1 (
    .Clock(delay_1_delayed_clock), .Reset(or_1_out), .Enable(Enable), .Q0(move_counter_2_disk_1_q0),
    .Q1(move_counter_2_disk_1_q1));
  T_Flip_Flop t_ff_7 (.clk(and_11_out), .T(1'b1), .Q(out_13), .reset(or_1_out));  // open: Qn, preset, en
  and and_12 (and_12_out, not_1_out, out_13);
  or or_1 (or_1_out, Reset, and_12_out);
endmodule

module Gray_Code_Counter_2_disk (
  input  Clock,
  input  Reset,
  input  Enable,
  output Q2,
  output Q1
);

  wire d_ff_1_q, d_ff_1_qn, d_ff_2_qn;

  D_Flip_Flop d_ff_1 (
    .clk(Clock), .D(d_ff_1_qn), .Q(d_ff_1_q), .Qn(d_ff_1_qn), .en(Enable), .reset(Reset));  // open: preset
  D_Flip_Flop d_ff_2 (
    .clk(d_ff_1_qn), .D(d_ff_2_qn), .Q(Q2), .Qn(d_ff_2_qn), .en(Enable), .reset(Reset));  // open: preset
  xor xor_1 (Q1, d_ff_1_q, Q2);
endmodule

module PIPO_Shift_Register_2_disk (
  input  Clock,
  input  I1,
  input  I0,
  input  Clear,
  input  Enable,
  output Q1,
  output Q0
);

  D_Flip_Flop d_ff_1 (.clk(Clock), .D(I1), .Q(Q1), .en(Enable), .reset(Clear));  // open: Qn, preset
  D_Flip_Flop d_ff_2 (.clk(Clock), .D(I0), .Q(Q0), .en(Enable), .reset(Clear));  // open: Qn, preset
endmodule

module Disk_Size_2_disk (
  input  Clock,
  input  Clear,
  input  Enable,
  output Disk_Medium,
  output Disk_Small
);

  wire gray_code_counter_2_disk_1_q1, gray_code_counter_2_disk_1_q2, pipo_shift_register_2_disk_1_q0,
       pipo_shift_register_2_disk_1_q1;

  Gray_Code_Counter_2_disk gray_code_counter_2_disk_1 (
    .Clock(Clock), .Reset(Clear), .Enable(Enable), .Q2(gray_code_counter_2_disk_1_q2),
    .Q1(gray_code_counter_2_disk_1_q1));
  xor xor_1 (Disk_Medium, gray_code_counter_2_disk_1_q2, pipo_shift_register_2_disk_1_q1);
  PIPO_Shift_Register_2_disk pipo_shift_register_2_disk_1 (
    .Clock(Clock), .I1(gray_code_counter_2_disk_1_q2), .I0(gray_code_counter_2_disk_1_q1), .Clear(Clear),
    .Enable(Enable), .Q1(pipo_shift_register_2_disk_1_q1), .Q0(pipo_shift_register_2_disk_1_q0));
  xor xor_2 (Disk_Small, gray_code_counter_2_disk_1_q1, pipo_shift_register_2_disk_1_q0);
endmodule

module Preset_generator (
  input  in_1,
  input  in_2,
  input  in_3,
  input  in_4,
  output out_5,
  output out_6,
  output out_7
);

  and and_1 (out_5, in_1, in_2);
  and and_2 (out_6, in_1, in_3);
  and and_3 (out_7, in_1, in_4);
endmodule

module Edge_finder (
  input  in_1,
  output out_2
);

  wire not_1_out, not_2_out, not_3_out;

  not not_1 (not_1_out, in_1);
  not not_2 (not_2_out, not_1_out);
  not not_3 (not_3_out, not_2_out);
  and and_1 (out_2, in_1, not_3_out);
endmodule

module Move_counter_2_disk (
  input  Clock,
  input  Reset,
  input  Enable,
  output Q0,
  output Q1
);

  T_Flip_Flop t_ff_1 (.clk(Clock), .T(1'b1), .Q(Q0), .reset(Reset), .en(Enable));  // open: Qn, preset
  T_Flip_Flop t_ff_2 (.clk(Clock), .T(Q0), .Q(Q1), .reset(Reset), .en(Enable));  // open: Qn, preset
endmodule

module Delay (
  input  Clock,
  output Delayed_Clock
);

  wire d_ff_1_q, d_ff_2_q;

  D_Flip_Flop #(.trigger("high")) d_ff_1 (.clk(1'b1), .D(Clock), .Q(d_ff_1_q));  // open: Qn, preset, en, reset
  D_Flip_Flop #(.trigger("high")) d_ff_2 (.clk(1'b1), .D(d_ff_1_q), .Q(d_ff_2_q));  // open: Qn, preset, en, reset
  D_Flip_Flop #(.trigger("high")) d_ff_3 (.clk(1'b1), .D(d_ff_2_q), .Q(Delayed_Clock));  // open: Qn, preset, en, reset
endmodule
